// Logisim project 21_bit_ALU.circ as structural Verilog: 11 circuits, main circuit main
module main (
  input  Control1,
  input  Control_2,
  input  Control0,
  input  [20:0] A,
  input  [20:0] B,
  output [20:0] Result,
  output Zero,
  output Negative,
  output Overflow,
  output Carry
);

  wire n21_bit_reduce_or_1_output;
  wire [20:0] add_sub_1_result, multiplexer_1_out, multiplexer_2_out, n21_bit_and_1_result,
       n21_bit_nor_1_result, n21_bit_or_1_result;

  _21_BIT_NOR u_21_bit_nor_1 (.A(A), .B(A), .Result(n21_bit_nor_1_result));
  _21_BIT_AND u_21_bit_and_1 (.A(A), .B(B), .Result(n21_bit_and_1_result));
  _21_BIT_OR u_21_bit_or_1 (.A(A), .B(B), .Result(n21_bit_or_1_result));
  ADD_SUB add_sub_1 (.Sub(Control0), .A(A), .B(B), .Result(add_sub_1_result), .Carry(Carry), .Overflow(Overflow));
  Multiplexer #(.width(21), .enable("false")) multiplexer_1 (
    .in0(n21_bit_and_1_result), .in1(n21_bit_or_1_result), .out(multiplexer_1_out), .sel(Control0));
  Multiplexer #(.width(21), .enable("false")) multiplexer_2 (
    .in0(multiplexer_1_out), .in1(add_sub_1_result), .out(multiplexer_2_out), .sel(Control1));
  Multiplexer #(.width(21), .enable("false")) multiplexer_3 (
    .in0(multiplexer_2_out), .in1(n21_bit_nor_1_result), .out(Result), .sel(Control_2));
  _21_BIT_OUT u_21_bit_out_1 (.INPUT(Result), ._21TH_BIT(Negative));
  _21_BIT_REDUCE_OR u_21_bit_reduce_or_1 (.A(Result), .OUTPUT(n21_bit_reduce_or_1_output));
  not not_1 (Zero, n21_bit_reduce_or_1_output);
endmodule

// 21_Bit_And
module _21_BIT_AND (
  input  [20:0] A,
  input  [20:0] B,
  output [20:0] Result
);

  assign Result = A & B;  // AND_Gate and_1, 21 bits wide
endmodule

// 21_Bit_Or
module _21_BIT_OR (
  input  [20:0] A,
  input  [20:0] B,
  output [20:0] Result
);

  assign Result = A | B;  // OR_Gate or_1, 21 bits wide
endmodule

module FULL_ADDER (
  input  CARRY_IN,
  input  A,
  input  B,
  output RESULT,
  output CARRY_OUT
);

  wire and_1_out, and_2_out, xor_1_out;

  and and_1 (and_1_out, A, B);
  xor xor_1 (xor_1_out, A, B);
  and and_2 (and_2_out, xor_1_out, CARRY_IN);
  or or_1 (CARRY_OUT, and_2_out, and_1_out);
  xor xor_2 (RESULT, CARRY_IN, xor_1_out);
endmodule

module _21_BIT_REDUCE_OR (
  input  [20:0] A,
  output OUTPUT
);

  or or_1 (OUTPUT, A[0], A[1], A[2], A[3], A[4], A[5], A[6], A[7], A[8], A[9], A[10], A[11], A[12], A[13], A[14], A[15], A[16], A[17], A[18], A[19], A[20]);
endmodule

// 21th
module _21_BIT_OUT (
  input  [20:0] INPUT,
  output _21TH_BIT
);


  assign _21TH_BIT = INPUT[20];
endmodule

// XOR
module _21_BIT_XOR (
  input  in_1,
  input  [20:0] B,
  output [20:0] RESULT
);

  wire [20:0] bit_extender_1_out;

  assign bit_extender_1_out = {{20{in_1}}, in_1};  // Bit_Extender bit_extender_1
  assign RESULT = bit_extender_1_out ^ B;  // XOR_Gate xor_1, 21 bits wide
endmodule

// 21_Bit_Add/Sub
module ADD_SUB (
  input  Sub,
  input  [20:0] A,
  input  [20:0] B,
  output [20:0] Result,
  output Carry,
  output Overflow
);

  wire and_1_out, and_2_out, n21_bit_out_1__21th_bit, n21_bit_out_2__21th_bit, n21_bit_out_3__21th_bit,
       not_1_out, not_2_out, not_3_out;
  wire [20:0] n21_bit_xor_1_result;

  _21_BIT_OUT u_21_bit_out_1 (.INPUT(A), ._21TH_BIT(n21_bit_out_1__21th_bit));
  _21_BIT_OUT u_21_bit_out_2 (.INPUT(n21_bit_xor_1_result), ._21TH_BIT(n21_bit_out_2__21th_bit));
  not not_1 (not_1_out, n21_bit_out_1__21th_bit);
  _21_BIT_XOR u_21_bit_xor_1 (.in_1(Sub), .B(B), .RESULT(n21_bit_xor_1_result));
  not not_2 (not_2_out, n21_bit_out_2__21th_bit);
  _21_BIT_FULL_ADDER u_21_bit_full_adder_1 (
    .A(A), .B(n21_bit_xor_1_result), .Carry_in(Sub), .Carry(Carry), .Result(Result));
  _21_BIT_OUT u_21_bit_out_3 (.INPUT(Result), ._21TH_BIT(n21_bit_out_3__21th_bit));
  not not_3 (not_3_out, n21_bit_out_3__21th_bit);
  and and_1 (and_1_out, not_3_out, n21_bit_out_1__21th_bit, n21_bit_out_2__21th_bit);
  and and_2 (and_2_out, n21_bit_out_3__21th_bit, not_2_out, not_1_out);
  or or_1 (Overflow, and_1_out, and_2_out);
endmodule

module add_sub (
  input  [20:0] A,
  input  in_2,
  input  in_3,
  input  in_4,
  input  in_5,
  input  [20:0] B,
  input  [20:0] C,
  input  in_8,
  input  in_9,
  input  B_2,
  input  in_11,
  input  [20:0] D,
  output out_13
);

  wire clock_1_out;
  wire [20:0] A_q, B_q, C_q, D_q, demultiplexer_1_out0, demultiplexer_1_out1, demultiplexer_1_out2,
       demultiplexer_1_out3, multiplexer_1_out, multiplexer_2_out, multiplexer_3_out, multiplexer_4_out,
       multiplexer_5_out, multiplexer_6_out, n21_bit_full_adder_1_result;

  Multiplexer #(.width(21), .enable("false")) multiplexer_1 (
    .in0(A), .in1(demultiplexer_1_out0), .out(multiplexer_1_out), .sel(in_4));
  Multiplexer #(.width(21), .enable("false")) multiplexer_2 (
    .in0(B), .in1(demultiplexer_1_out1), .out(multiplexer_2_out), .sel(in_4));
  Multiplexer #(.width(21), .enable("false")) multiplexer_3 (
    .in0(C), .in1(demultiplexer_1_out2), .out(multiplexer_3_out), .sel(in_4));
  Multiplexer #(.width(21), .enable("false")) multiplexer_4 (
    .in0(D), .in1(demultiplexer_1_out3), .out(multiplexer_4_out), .sel(in_4));
  Register #(.width(21)) u_A (.D(multiplexer_1_out), .en(1'b1), .Q(A_q), .clk(clock_1_out));  // open: clr
  Clock clock_1 (.out(clock_1_out));
  Register #(.width(21)) u_B (.D(multiplexer_2_out), .en(1'b1), .Q(B_q), .clk(clock_1_out));  // open: clr
  Register #(.width(21)) u_C (.D(multiplexer_3_out), .en(1'b1), .Q(C_q), .clk(clock_1_out));  // open: clr
  Register #(.width(21)) u_D (.D(multiplexer_4_out), .en(1'b1), .Q(D_q), .clk(clock_1_out));  // open: clr
  Multiplexer #(.select(2), .width(21), .enable("false")) multiplexer_5 (
    .in0(A_q), .in1(B_q), .in2(C_q), .in3(D_q), .out(multiplexer_5_out), .sel({in_2, in_3}));
  Multiplexer #(.select(2), .width(21), .enable("false")) multiplexer_6 (
    .in0(A_q), .in1(B_q), .in2(B_q), .in3(D_q), .out(multiplexer_6_out), .sel({in_11, B_2}));
  _21_BIT_FULL_ADDER u_21_bit_full_adder_1 (
    .A(multiplexer_5_out), .B(multiplexer_6_out), .Carry_in(in_5), .Carry(out_13),
    .Result(n21_bit_full_adder_1_result));
  Demultiplexer #(.select(2), .width(21), .enable("false")) demultiplexer_1 (
    .out0(demultiplexer_1_out0), .out1(demultiplexer_1_out1), .out2(demultiplexer_1_out2),
    .out3(demultiplexer_1_out3), .in(n21_bit_full_adder_1_result), .sel({in_9, in_8}));

  // Notes on the sheet:
  //    A
  //   select output
  //   00 - A
  //   01 - B
  //   10 - C
  //   11 - D
endmodule

// 21_Bit_Adder
module _21_BIT_FULL_ADDER (
  input  Carry_in,
  input  [20:0] A,
  input  [20:0] B,
  output [20:0] Result,
  output Carry
);

  wire full_adder_1_carry_out, full_adder_2_carry_out, full_adder_3_carry_out, full_adder_4_carry_out,
       full_adder_5_carry_out, full_adder_6_carry_out, full_adder_7_carry_out, full_adder_8_carry_out,
       full_adder_9_carry_out, full_adder_10_carry_out, full_adder_11_carry_out, full_adder_12_carry_out,
       full_adder_13_carry_out, full_adder_14_carry_out, full_adder_15_carry_out, full_adder_16_carry_out,
       full_adder_17_carry_out, full_adder_18_carry_out, full_adder_19_carry_out, full_adder_20_carry_out;

  FULL_ADDER full_adder_1 (
    .A(A[0]), .B(B[0]), .CARRY_IN(Carry_in), .CARRY_OUT(full_adder_1_carry_out), .RESULT(Result[0]));
  FULL_ADDER full_adder_2 (
    .A(A[1]), .B(B[1]), .CARRY_IN(full_adder_1_carry_out), .CARRY_OUT(full_adder_2_carry_out),
    .RESULT(Result[1]));
  FULL_ADDER full_adder_3 (
    .A(A[2]), .B(B[2]), .CARRY_IN(full_adder_2_carry_out), .CARRY_OUT(full_adder_3_carry_out),
    .RESULT(Result[2]));
  FULL_ADDER full_adder_4 (
    .A(A[3]), .B(B[3]), .CARRY_IN(full_adder_3_carry_out), .CARRY_OUT(full_adder_4_carry_out),
    .RESULT(Result[3]));
  FULL_ADDER full_adder_5 (
    .A(A[4]), .B(B[4]), .CARRY_IN(full_adder_4_carry_out), .CARRY_OUT(full_adder_5_carry_out),
    .RESULT(Result[4]));
  FULL_ADDER full_adder_6 (
    .A(A[5]), .B(B[5]), .CARRY_IN(full_adder_5_carry_out), .CARRY_OUT(full_adder_6_carry_out),
    .RESULT(Result[5]));
  FULL_ADDER full_adder_7 (
    .A(A[6]), .B(B[6]), .CARRY_IN(full_adder_6_carry_out), .CARRY_OUT(full_adder_7_carry_out),
    .RESULT(Result[6]));
  FULL_ADDER full_adder_8 (
    .A(A[7]), .B(B[7]), .CARRY_IN(full_adder_7_carry_out), .CARRY_OUT(full_adder_8_carry_out),
    .RESULT(Result[7]));
  FULL_ADDER full_adder_9 (
    .A(A[8]), .B(B[8]), .CARRY_IN(full_adder_8_carry_out), .CARRY_OUT(full_adder_9_carry_out),
    .RESULT(Result[8]));
  FULL_ADDER full_adder_10 (
    .A(A[9]), .B(B[9]), .CARRY_IN(full_adder_9_carry_out), .CARRY_OUT(full_adder_10_carry_out),
    .RESULT(Result[9]));
  FULL_ADDER full_adder_11 (
    .A(A[10]), .B(B[10]), .CARRY_IN(full_adder_10_carry_out), .CARRY_OUT(full_adder_11_carry_out),
    .RESULT(Result[10]));
  FULL_ADDER full_adder_12 (
    .A(A[11]), .B(B[11]), .CARRY_IN(full_adder_11_carry_out), .CARRY_OUT(full_adder_12_carry_out),
    .RESULT(Result[11]));
  FULL_ADDER full_adder_13 (
    .A(A[12]), .B(B[12]), .CARRY_IN(full_adder_12_carry_out), .CARRY_OUT(full_adder_13_carry_out),
    .RESULT(Result[12]));
  FULL_ADDER full_adder_14 (
    .A(A[13]), .B(B[13]), .CARRY_IN(full_adder_13_carry_out), .CARRY_OUT(full_adder_14_carry_out),
    .RESULT(Result[13]));
  FULL_ADDER full_adder_15 (
    .A(A[14]), .B(B[14]), .CARRY_IN(full_adder_14_carry_out), .CARRY_OUT(full_adder_15_carry_out),
    .RESULT(Result[14]));
  FULL_ADDER full_adder_16 (
    .A(A[15]), .B(B[15]), .CARRY_IN(full_adder_15_carry_out), .CARRY_OUT(full_adder_16_carry_out),
    .RESULT(Result[15]));
  FULL_ADDER full_adder_17 (
    .A(A[16]), .B(B[16]), .CARRY_IN(full_adder_16_carry_out), .CARRY_OUT(full_adder_17_carry_out),
    .RESULT(Result[16]));
  FULL_ADDER full_adder_18 (
    .A(B[17]), .B(A[17]), .CARRY_IN(full_adder_17_carry_out), .CARRY_OUT(full_adder_18_carry_out),
    .RESULT(Result[17]));
  FULL_ADDER full_adder_19 (
    .A(A[18]), .B(B[18]), .CARRY_IN(full_adder_18_carry_out), .CARRY_OUT(full_adder_19_carry_out),
    .RESULT(Result[18]));
  FULL_ADDER full_adder_20 (
    .A(A[19]), .B(B[19]), .CARRY_IN(full_adder_19_carry_out), .CARRY_OUT(full_adder_20_carry_out),
    .RESULT(Result[19]));
  FULL_ADDER full_adder_21 (
    .A(A[20]), .B(B[20]), .CARRY_IN(full_adder_20_carry_out), .CARRY_OUT(Carry), .RESULT(Result[20]));

  // Other names for the same wires on the sheet: res0 = Result[0]; res1 = Result[1]
endmodule

module _21_BIT_NOR (
  input  [20:0] A,
  input  [20:0] B,
  output [20:0] Result
);

  assign Result = ~(A | B);  // NOR_Gate nor_1, 21 bits wide
endmodule
