// Logisim project ALU_21_bit_assignment_2_2107055.circ as structural Verilog: 10 circuits, main circuit main
module main (
  input  control0,
  input  control1,
  input  [20:0] A,
  input  [20:0] B,
  output [20:0] ans,
  output neg,
  output zero,
  output carry,
  output overflow
);

  wire bit21recude_1_ouptut;
  wire [20:0] add_sub_1_result, and_21bit_1_output_and, multiplexer_1_out, or_21bit_1_output_or;

  AND_21bit and_21bit_1 (.A(A), .B(B), .Output_AND(and_21bit_1_output_and));
  OR_21bit or_21bit_1 (.A(A), .B(B), .Output_OR(or_21bit_1_output_or));
  add_sub add_sub_1 (.operation(control0), .A(A), .B(B), .result(add_sub_1_result), .carry(carry), .overflow(overflow));
  Multiplexer #(.width(21)) multiplexer_1 (
    .in0(and_21bit_1_output_and), .in1(or_21bit_1_output_or), .out(multiplexer_1_out), .sel(control0));
  Multiplexer #(.width(21)) multiplexer_2 (.in0(multiplexer_1_out), .in1(add_sub_1_result), .out(ans), .sel(control1));
  bit21recude bit21recude_1 (.in_1(ans), .ouptut(bit21recude_1_ouptut));
  bits21out bits21out_1 (.in_1(ans), .bit_20(neg));
  not not_1 (zero, bit21recude_1_ouptut);
endmodule

module AND_21bit (
  input  [20:0] A,
  input  [20:0] B,
  output [20:0] Output_AND
);

  assign Output_AND = A & B;  // AND_Gate and_1, 21 bits wide
endmodule

module OR_21bit (
  input  [20:0] A,
  input  [20:0] B,
  output [20:0] Output_OR
);

  assign Output_OR = A | B;  // OR_Gate or_1, 21 bits wide
endmodule

module Full_Adder_2bit (
  input  A,
  input  B,
  input  Cin,
  output Sum,
  output Carry
);

  wire and_1_out, and_2_out, xor_1_out;

  xor xor_1 (xor_1_out, B, A);
  and and_1 (and_1_out, xor_1_out, Cin);
  and and_2 (and_2_out, B, A);
  xor xor_2 (Sum, xor_1_out, Cin);
  or or_1 (Carry, and_1_out, and_2_out);
endmodule

module Adder_21bit (
  input  A0,
  input  B0,
  input  Cin,
  input  A1,
  input  B1,
  input  A2,
  input  B2,
  input  A3,
  input  B3,
  input  A4,
  input  B4,
  input  A5,
  input  B5,
  input  A6,
  input  B6,
  input  A7,
  input  B7,
  input  A8,
  input  B8,
  input  A9,
  input  B9,
  input  A10,
  input  B10,
  input  A11,
  input  B11,
  input  A12,
  input  B12,
  input  A13,
  input  B13,
  input  A14,
  input  B14,
  input  A15,
  input  B15,
  input  A16,
  input  B16,
  input  A17,
  input  B17,
  input  A18,
  input  B18,
  input  A19,
  input  B19,
  input  A20,
  input  B20,
  output R0,
  output R1,
  output R2,
  output R3,
  output R4,
  output R5,
  output R6,
  output R7,
  output R8,
  output R9,
  output R10,
  output R11,
  output R12,
  output R13,
  output R14,
  output R15,
  output R16,
  output R17,
  output R18,
  output R19,
  output R20,
  output Cout
);

  wire full_adder_2bit_1_carry, full_adder_2bit_2_carry, full_adder_2bit_3_carry, full_adder_2bit_4_carry,
       full_adder_2bit_5_carry, full_adder_2bit_6_carry, full_adder_2bit_7_carry, full_adder_2bit_8_carry,
       full_adder_2bit_9_carry, full_adder_2bit_10_carry, full_adder_2bit_11_carry, full_adder_2bit_12_carry,
       full_adder_2bit_13_carry, full_adder_2bit_14_carry, full_adder_2bit_15_carry,
       full_adder_2bit_16_carry, full_adder_2bit_17_carry, full_adder_2bit_18_carry,
       full_adder_2bit_19_carry, full_adder_2bit_20_carry;

  Full_Adder_2bit full_adder_2bit_1 (.A(A0), .B(B0), .Cin(Cin), .Sum(R0), .Carry(full_adder_2bit_1_carry));
  Full_Adder_2bit full_adder_2bit_2 (
    .A(A1), .B(B1), .Cin(full_adder_2bit_1_carry), .Sum(R1), .Carry(full_adder_2bit_2_carry));
  Full_Adder_2bit full_adder_2bit_3 (
    .A(A2), .B(B2), .Cin(full_adder_2bit_2_carry), .Sum(R2), .Carry(full_adder_2bit_3_carry));
  Full_Adder_2bit full_adder_2bit_4 (
    .A(A3), .B(B3), .Cin(full_adder_2bit_3_carry), .Sum(R3), .Carry(full_adder_2bit_4_carry));
  Full_Adder_2bit full_adder_2bit_5 (
    .A(A4), .B(B4), .Cin(full_adder_2bit_4_carry), .Sum(R4), .Carry(full_adder_2bit_5_carry));
  Full_Adder_2bit full_adder_2bit_6 (
    .A(A5), .B(B5), .Cin(full_adder_2bit_5_carry), .Sum(R5), .Carry(full_adder_2bit_6_carry));
  Full_Adder_2bit full_adder_2bit_7 (
    .A(A6), .B(B6), .Cin(full_adder_2bit_6_carry), .Sum(R6), .Carry(full_adder_2bit_7_carry));
  Full_Adder_2bit full_adder_2bit_8 (
    .A(A7), .B(B7), .Cin(full_adder_2bit_7_carry), .Sum(R7), .Carry(full_adder_2bit_8_carry));
  Full_Adder_2bit full_adder_2bit_9 (
    .A(A8), .B(B8), .Cin(full_adder_2bit_8_carry), .Sum(R8), .Carry(full_adder_2bit_9_carry));
  Full_Adder_2bit full_adder_2bit_10 (
    .A(A9), .B(B9), .Cin(full_adder_2bit_9_carry), .Sum(R9), .Carry(full_adder_2bit_10_carry));
  Full_Adder_2bit full_adder_2bit_11 (
    .A(A10), .B(B10), .Cin(full_adder_2bit_10_carry), .Sum(R10), .Carry(full_adder_2bit_11_carry));
  Full_Adder_2bit full_adder_2bit_12 (
    .A(A11), .B(B11), .Cin(full_adder_2bit_11_carry), .Sum(R11), .Carry(full_adder_2bit_12_carry));
  Full_Adder_2bit full_adder_2bit_13 (
    .A(A12), .B(B12), .Cin(full_adder_2bit_12_carry), .Sum(R12), .Carry(full_adder_2bit_13_carry));
  Full_Adder_2bit full_adder_2bit_14 (
    .A(A13), .B(B13), .Cin(full_adder_2bit_13_carry), .Sum(R13), .Carry(full_adder_2bit_14_carry));
  Full_Adder_2bit full_adder_2bit_15 (
    .A(A14), .B(B14), .Cin(full_adder_2bit_14_carry), .Sum(R14), .Carry(full_adder_2bit_15_carry));
  Full_Adder_2bit full_adder_2bit_16 (
    .A(A15), .B(B15), .Cin(full_adder_2bit_15_carry), .Sum(R15), .Carry(full_adder_2bit_16_carry));
  Full_Adder_2bit full_adder_2bit_17 (
    .A(A16), .B(B16), .Cin(full_adder_2bit_16_carry), .Sum(R16), .Carry(full_adder_2bit_17_carry));
  Full_Adder_2bit full_adder_2bit_18 (
    .A(A17), .B(B17), .Cin(full_adder_2bit_17_carry), .Sum(R17), .Carry(full_adder_2bit_18_carry));
  Full_Adder_2bit full_adder_2bit_19 (
    .A(A18), .B(B18), .Cin(full_adder_2bit_18_carry), .Sum(R18), .Carry(full_adder_2bit_19_carry));
  Full_Adder_2bit full_adder_2bit_20 (
    .A(A19), .B(B19), .Cin(full_adder_2bit_19_carry), .Sum(R19), .Carry(full_adder_2bit_20_carry));
  Full_Adder_2bit full_adder_2bit_21 (.A(A20), .B(B20), .Cin(full_adder_2bit_20_carry), .Sum(R20), .Carry(Cout));
endmodule

module Addition_21bit (
  input  Cin,
  input  [20:0] A,
  input  [20:0] B,
  output [20:0] sum,
  output Cout
);

  Adder_21bit adder_21bit_1 (
    .A0(A[0]), .B0(B[0]), .Cin(Cin), .A1(A[1]), .B1(B[1]), .A2(A[2]), .B2(B[2]), .A3(A[3]), .B3(B[3]),
    .A4(A[4]), .B4(B[4]), .A5(A[5]), .B5(B[5]), .A6(A[6]), .B6(B[6]), .A7(A[7]), .B7(B[7]), .A8(A[8]),
    .B8(B[8]), .A9(A[9]), .B9(B[9]), .A10(A[10]), .B10(B[10]), .A11(A[11]), .B11(B[11]), .A12(A[12]),
    .B12(B[12]), .A13(A[13]), .B13(B[13]), .A14(A[14]), .B14(B[14]), .A15(A[15]), .B15(B[15]), .A16(A[16]),
    .B16(B[16]), .A17(A[17]), .B17(B[17]), .A18(A[18]), .B18(B[18]), .A19(A[19]), .B19(B[19]), .A20(A[20]),
    .B20(B[20]), .R0(sum[0]), .R1(sum[1]), .R2(sum[2]), .R3(sum[3]), .R4(sum[4]), .R5(sum[5]), .R6(sum[6]),
    .R7(sum[7]), .R8(sum[8]), .R9(sum[9]), .R10(sum[10]), .R11(sum[11]), .R12(sum[12]), .R13(sum[13]),
    .R14(sum[14]), .R15(sum[15]), .R16(sum[16]), .R17(sum[17]), .R18(sum[18]), .R19(sum[19]), .R20(sum[20]),
    .Cout(Cout));
endmodule

module xor21bit (
  input  control,
  input  [20:0] in_2,
  output [20:0] bit_output
);

  wire [20:0] bit_extender_1_out;

  assign bit_extender_1_out = {{20{control}}, control};  // Bit_Extender bit_extender_1
  assign bit_output = bit_extender_1_out ^ in_2;  // XOR_Gate xor_1, 21 bits wide
endmodule

module bits21out (
  input  [20:0] in_1,
  output bit_20
);


  assign bit_20 = in_1[20];
endmodule

module bit21recude (
  input  [20:0] in_1,
  output ouptut
);

  or or_1 (ouptut, in_1[0], in_1[1], in_1[2], in_1[3], in_1[4], in_1[5], in_1[6], in_1[7], in_1[8], in_1[9], in_1[10], in_1[11], in_1[12], in_1[13], in_1[14], in_1[15], in_1[16], in_1[17], in_1[18], in_1[19], in_1[20]);
endmodule

module add_sub (
  input  operation,
  input  [20:0] A,
  input  [20:0] B,
  output [20:0] result,
  output carry,
  output overflow
);

  wire and_1_out, and_2_out, bits21out_1_bit_20, bits21out_2_bit_20, bits21out_3_bit_20, not_1_out,
       not_2_out, not_3_out;
  wire [20:0] xor21bit_1_bit_output;

  bits21out bits21out_1 (.in_1(A), .bit_20(bits21out_1_bit_20));
  not not_1 (not_1_out, bits21out_1_bit_20);
  xor21bit xor21bit_1 (.control(operation), .in_2(B), .bit_output(xor21bit_1_bit_output));
  bits21out bits21out_2 (.in_1(xor21bit_1_bit_output), .bit_20(bits21out_2_bit_20));
  Addition_21bit addition_21bit_1 (.Cin(operation), .A(A), .B(xor21bit_1_bit_output), .sum(result), .Cout(carry));
  not not_2 (not_2_out, bits21out_2_bit_20);
  bits21out bits21out_3 (.in_1(result), .bit_20(bits21out_3_bit_20));
  not not_3 (not_3_out, bits21out_3_bit_20);
  and and_1 (and_1_out, not_3_out, bits21out_1_bit_20, bits21out_2_bit_20);
  and and_2 (and_2_out, bits21out_3_bit_20, not_2_out, not_1_out);
  or or_1 (overflow, and_1_out, and_2_out);
endmodule
