// Logisim project 32-bit-ALU.circ as structural Verilog: 10 circuits, main circuit main
module main (
  input  Control0,
  input  Control1,
  input  [31:0] A,
  input  [31:0] B,
  output [31:0] Result,
  output Zero,
  output Negative,
  output Overflow,
  output Carry
);

  wire l_32_bit_reduce_or_303f46c2_1_output;
  wire [31:0] add_sub_1_result, l_32_bit_and_a491032d_1_result, l_32_bit_or_47391bfa_1_result,
       multiplexer_1_out;

  L_32_bit_and_a491032d l_32_bit_and_a491032d_1 (.A(A), .B(B), .Result(l_32_bit_and_a491032d_1_result));
  L_32_bit_OR_47391bfa l_32_bit_or_47391bfa_1 (.A(A), .B(B), .Result(l_32_bit_or_47391bfa_1_result));
  Add_sub add_sub_1 (.A(A), .B(B), .Sub(Control0), .Overflow(Overflow), .Carry(Carry), .Result(add_sub_1_result));
  Multiplexer #(.width(32)) multiplexer_1 (
    .in0(l_32_bit_and_a491032d_1_result), .in1(l_32_bit_or_47391bfa_1_result), .out(multiplexer_1_out),
    .sel(Control0));
  Multiplexer #(.width(32)) multiplexer_2 (
    .in0(multiplexer_1_out), .in1(add_sub_1_result), .out(Result), .sel(Control1));
  L_31th_bit_out_54576267 l_31th_bit_out_54576267_1 (.Input(Result), .L_31th_bit_03e70a82(Negative));
  L_32_bit_reduce_or_303f46c2 l_32_bit_reduce_or_303f46c2_1 (
    .Input(Result), .Output(l_32_bit_reduce_or_303f46c2_1_output));
  not not_1 (Zero, l_32_bit_reduce_or_303f46c2_1_output);
endmodule

// 32-bit AND
module L_32_bit_and_a491032d (
  input  [31:0] A,
  input  [31:0] B,
  output [31:0] Result
);

  assign Result = A & B;  // AND_Gate and_1, 32 bits wide
endmodule

// 32-bit OR
module L_32_bit_OR_47391bfa (
  input  [31:0] A,
  input  [31:0] B,
  output [31:0] Result
);

  assign Result = A | B;  // OR_Gate or_1, 32 bits wide
endmodule

module Full_adder (
  input  Carry_in_b536e4fd,
  input  A,
  input  B,
  output Result,
  output Carry_out_0c8372ad
);

  wire and_1_out, and_2_out, xor_1_out;

  and and_1 (and_1_out, B, A);
  xor xor_1 (xor_1_out, A, B);
  or or_1 (Carry_out_0c8372ad, and_1_out, and_2_out);
  and and_2 (and_2_out, xor_1_out, Carry_in_b536e4fd);
  xor xor_2 (Result, Carry_in_b536e4fd, xor_1_out);
endmodule

module L_32_bit_full_adder_b6ceec0b (
  input  Carry_in_b536e4fd,
  input  A0,
  input  B0,
  input  A1,
  input  B1,
  input  A2,
  input  B2,
  input  A3,
  input  B3,
  input  A4,
  input  B4,
  input  A5,
  input  B5,
  input  A6,
  input  B6,
  input  A7,
  input  B7,
  input  A8,
  input  B8,
  input  A9,
  input  B9,
  input  A10,
  input  B10,
  input  A11,
  input  B11,
  input  A12,
  input  B12,
  input  A13,
  input  B13,
  input  A14,
  input  B14,
  input  A15,
  input  B15,
  input  A16,
  input  B16,
  input  A17,
  input  B17,
  input  A18,
  input  B18,
  input  A19,
  input  B19,
  input  A20,
  input  B20,
  input  A21,
  input  B21,
  input  A22,
  input  B22,
  input  A23,
  input  B23,
  input  A24,
  input  B24,
  input  A25,
  input  B25,
  input  A26,
  input  B26,
  input  A27,
  input  B27,
  input  A28,
  input  B28,
  input  A29,
  input  B29,
  input  A30,
  input  B30,
  input  A31,
  input  B31,
  output Result0,
  output Result1,
  output Result2,
  output Result3,
  output Result4,
  output Result5,
  output Result6,
  output Result7,
  output Result8,
  output Result9,
  output Result10,
  output Result11,
  output Result12,
  output Result13,
  output Result14,
  output Result15,
  output Result16,
  output Result17,
  output Result18,
  output Result19,
  output Result20,
  output Result21,
  output Result22,
  output Result23,
  output Result24,
  output Result25,
  output Result26,
  output Result27,
  output Result28,
  output Result29,
  output Result30,
  output Result31,
  output Carry
);

  wire full_adder_1_carry_out_0c8372ad, full_adder_2_carry_out_0c8372ad, full_adder_3_carry_out_0c8372ad,
       full_adder_4_carry_out_0c8372ad, full_adder_5_carry_out_0c8372ad, full_adder_6_carry_out_0c8372ad,
       full_adder_7_carry_out_0c8372ad, full_adder_8_carry_out_0c8372ad, full_adder_9_carry_out_0c8372ad,
       full_adder_10_carry_out_0c8372ad, full_adder_11_carry_out_0c8372ad, full_adder_12_carry_out_0c8372ad,
       full_adder_13_carry_out_0c8372ad, full_adder_14_carry_out_0c8372ad, full_adder_15_carry_out_0c8372ad,
       full_adder_16_carry_out_0c8372ad, full_adder_17_carry_out_0c8372ad, full_adder_18_carry_out_0c8372ad,
       full_adder_19_carry_out_0c8372ad, full_adder_20_carry_out_0c8372ad, full_adder_21_carry_out_0c8372ad,
       full_adder_22_carry_out_0c8372ad, full_adder_23_carry_out_0c8372ad, full_adder_24_carry_out_0c8372ad,
       full_adder_25_carry_out_0c8372ad, full_adder_26_carry_out_0c8372ad, full_adder_27_carry_out_0c8372ad,
       full_adder_28_carry_out_0c8372ad, full_adder_29_carry_out_0c8372ad, full_adder_30_carry_out_0c8372ad,
       full_adder_31_carry_out_0c8372ad;

  Full_adder full_adder_1 (
    .A(A0), .B(B0), .Carry_in_b536e4fd(Carry_in_b536e4fd),
    .Carry_out_0c8372ad(full_adder_1_carry_out_0c8372ad), .Result(Result0));
  Full_adder full_adder_2 (
    .A(A1), .B(B1), .Carry_in_b536e4fd(full_adder_1_carry_out_0c8372ad),
    .Carry_out_0c8372ad(full_adder_2_carry_out_0c8372ad), .Result(Result1));
  Full_adder full_adder_3 (
    .A(A2), .B(B2), .Carry_in_b536e4fd(full_adder_2_carry_out_0c8372ad),
    .Carry_out_0c8372ad(full_adder_3_carry_out_0c8372ad), .Result(Result2));
  Full_adder full_adder_4 (
    .A(A3), .B(B3), .Carry_in_b536e4fd(full_adder_3_carry_out_0c8372ad),
    .Carry_out_0c8372ad(full_adder_4_carry_out_0c8372ad), .Result(Result3));
  Full_adder full_adder_5 (
    .A(A4), .B(B4), .Carry_in_b536e4fd(full_adder_4_carry_out_0c8372ad),
    .Carry_out_0c8372ad(full_adder_5_carry_out_0c8372ad), .Result(Result4));
  Full_adder full_adder_6 (
    .A(A5), .B(B5), .Carry_in_b536e4fd(full_adder_5_carry_out_0c8372ad),
    .Carry_out_0c8372ad(full_adder_6_carry_out_0c8372ad), .Result(Result5));
  Full_adder full_adder_7 (
    .A(A6), .B(B6), .Carry_in_b536e4fd(full_adder_6_carry_out_0c8372ad),
    .Carry_out_0c8372ad(full_adder_7_carry_out_0c8372ad), .Result(Result6));
  Full_adder full_adder_8 (
    .A(A7), .B(B7), .Carry_in_b536e4fd(full_adder_7_carry_out_0c8372ad),
    .Carry_out_0c8372ad(full_adder_8_carry_out_0c8372ad), .Result(Result7));
  Full_adder full_adder_9 (
    .A(A8), .B(B8), .Carry_in_b536e4fd(full_adder_8_carry_out_0c8372ad),
    .Carry_out_0c8372ad(full_adder_9_carry_out_0c8372ad), .Result(Result8));
  Full_adder full_adder_10 (
    .A(A9), .B(B9), .Carry_in_b536e4fd(full_adder_9_carry_out_0c8372ad),
    .Carry_out_0c8372ad(full_adder_10_carry_out_0c8372ad), .Result(Result9));
  Full_adder full_adder_11 (
    .A(A10), .B(B10), .Carry_in_b536e4fd(full_adder_10_carry_out_0c8372ad),
    .Carry_out_0c8372ad(full_adder_11_carry_out_0c8372ad), .Result(Result10));
  Full_adder full_adder_12 (
    .A(A11), .B(B11), .Carry_in_b536e4fd(full_adder_11_carry_out_0c8372ad),
    .Carry_out_0c8372ad(full_adder_12_carry_out_0c8372ad), .Result(Result11));
  Full_adder full_adder_13 (
    .A(A12), .B(B12), .Carry_in_b536e4fd(full_adder_12_carry_out_0c8372ad),
    .Carry_out_0c8372ad(full_adder_13_carry_out_0c8372ad), .Result(Result12));
  Full_adder full_adder_14 (
    .A(A13), .B(B13), .Carry_in_b536e4fd(full_adder_13_carry_out_0c8372ad),
    .Carry_out_0c8372ad(full_adder_14_carry_out_0c8372ad), .Result(Result13));
  Full_adder full_adder_15 (
    .A(A14), .B(B14), .Carry_in_b536e4fd(full_adder_14_carry_out_0c8372ad),
    .Carry_out_0c8372ad(full_adder_15_carry_out_0c8372ad), .Result(Result14));
  Full_adder full_adder_16 (
    .A(A15), .B(B15), .Carry_in_b536e4fd(full_adder_15_carry_out_0c8372ad),
    .Carry_out_0c8372ad(full_adder_16_carry_out_0c8372ad), .Result(Result15));
  Full_adder full_adder_17 (
    .A(A16), .B(B16), .Carry_in_b536e4fd(full_adder_16_carry_out_0c8372ad),
    .Carry_out_0c8372ad(full_adder_17_carry_out_0c8372ad), .Result(Result16));
  Full_adder full_adder_18 (
    .A(A17), .B(B17), .Carry_in_b536e4fd(full_adder_17_carry_out_0c8372ad),
    .Carry_out_0c8372ad(full_adder_18_carry_out_0c8372ad), .Result(Result17));
  Full_adder full_adder_19 (
    .A(A18), .B(B18), .Carry_in_b536e4fd(full_adder_18_carry_out_0c8372ad),
    .Carry_out_0c8372ad(full_adder_19_carry_out_0c8372ad), .Result(Result18));
  Full_adder full_adder_20 (
    .A(A19), .B(B19), .Carry_in_b536e4fd(full_adder_19_carry_out_0c8372ad),
    .Carry_out_0c8372ad(full_adder_20_carry_out_0c8372ad), .Result(Result19));
  Full_adder full_adder_21 (
    .A(A20), .B(B20), .Carry_in_b536e4fd(full_adder_20_carry_out_0c8372ad),
    .Carry_out_0c8372ad(full_adder_21_carry_out_0c8372ad), .Result(Result20));
  Full_adder full_adder_22 (
    .A(A21), .B(B21), .Carry_in_b536e4fd(full_adder_21_carry_out_0c8372ad),
    .Carry_out_0c8372ad(full_adder_22_carry_out_0c8372ad), .Result(Result21));
  Full_adder full_adder_23 (
    .A(A22), .B(B22), .Carry_in_b536e4fd(full_adder_22_carry_out_0c8372ad),
    .Carry_out_0c8372ad(full_adder_23_carry_out_0c8372ad), .Result(Result22));
  Full_adder full_adder_24 (
    .A(A23), .B(B23), .Carry_in_b536e4fd(full_adder_23_carry_out_0c8372ad),
    .Carry_out_0c8372ad(full_adder_24_carry_out_0c8372ad), .Result(Result23));
  Full_adder full_adder_25 (
    .A(A24), .B(B24), .Carry_in_b536e4fd(full_adder_24_carry_out_0c8372ad),
    .Carry_out_0c8372ad(full_adder_25_carry_out_0c8372ad), .Result(Result24));
  Full_adder full_adder_26 (
    .A(A25), .B(B25), .Carry_in_b536e4fd(full_adder_25_carry_out_0c8372ad),
    .Carry_out_0c8372ad(full_adder_26_carry_out_0c8372ad), .Result(Result25));
  Full_adder full_adder_27 (
    .A(A26), .B(B26), .Carry_in_b536e4fd(full_adder_26_carry_out_0c8372ad),
    .Carry_out_0c8372ad(full_adder_27_carry_out_0c8372ad), .Result(Result26));
  Full_adder full_adder_28 (
    .A(A27), .B(B27), .Carry_in_b536e4fd(full_adder_27_carry_out_0c8372ad),
    .Carry_out_0c8372ad(full_adder_28_carry_out_0c8372ad), .Result(Result27));
  Full_adder full_adder_29 (
    .A(A28), .B(B28), .Carry_in_b536e4fd(full_adder_28_carry_out_0c8372ad),
    .Carry_out_0c8372ad(full_adder_29_carry_out_0c8372ad), .Result(Result28));
  Full_adder full_adder_30 (
    .A(A29), .B(B29), .Carry_in_b536e4fd(full_adder_29_carry_out_0c8372ad),
    .Carry_out_0c8372ad(full_adder_30_carry_out_0c8372ad), .Result(Result29));
  Full_adder full_adder_31 (
    .A(A30), .B(B30), .Carry_in_b536e4fd(full_adder_30_carry_out_0c8372ad),
    .Carry_out_0c8372ad(full_adder_31_carry_out_0c8372ad), .Result(Result30));
  Full_adder full_adder_32 (
    .A(A31), .B(B31), .Carry_in_b536e4fd(full_adder_31_carry_out_0c8372ad), .Carry_out_0c8372ad(Carry),
    .Result(Result31));
endmodule

// 32-bit adder
module L_32_bit_full_adder_concise_37212314 (
  input  Carry_in_b536e4fd,
  input  [31:0] A,
  input  [31:0] B,
  output [31:0] Result,
  output Carry
);

  wire full_adder_1_carry_out_0c8372ad, full_adder_2_carry_out_0c8372ad, full_adder_3_carry_out_0c8372ad,
       full_adder_4_carry_out_0c8372ad, full_adder_5_carry_out_0c8372ad, full_adder_6_carry_out_0c8372ad,
       full_adder_7_carry_out_0c8372ad, full_adder_8_carry_out_0c8372ad, full_adder_9_carry_out_0c8372ad,
       full_adder_10_carry_out_0c8372ad, full_adder_11_carry_out_0c8372ad, full_adder_12_carry_out_0c8372ad,
       full_adder_13_carry_out_0c8372ad, full_adder_14_carry_out_0c8372ad, full_adder_15_carry_out_0c8372ad,
       full_adder_16_carry_out_0c8372ad, full_adder_17_carry_out_0c8372ad, full_adder_18_carry_out_0c8372ad,
       full_adder_19_carry_out_0c8372ad, full_adder_20_carry_out_0c8372ad, full_adder_21_carry_out_0c8372ad,
       full_adder_22_carry_out_0c8372ad, full_adder_23_carry_out_0c8372ad, full_adder_24_carry_out_0c8372ad,
       full_adder_25_carry_out_0c8372ad, full_adder_26_carry_out_0c8372ad, full_adder_27_carry_out_0c8372ad,
       full_adder_28_carry_out_0c8372ad, full_adder_29_carry_out_0c8372ad, full_adder_30_carry_out_0c8372ad,
       full_adder_31_carry_out_0c8372ad;

  Full_adder full_adder_1 (
    .A(A[0]), .B(B[0]), .Carry_in_b536e4fd(Carry_in_b536e4fd),
    .Carry_out_0c8372ad(full_adder_1_carry_out_0c8372ad), .Result(Result[0]));
  Full_adder full_adder_2 (
    .A(A[1]), .B(B[1]), .Carry_in_b536e4fd(full_adder_1_carry_out_0c8372ad),
    .Carry_out_0c8372ad(full_adder_2_carry_out_0c8372ad), .Result(Result[1]));
  Full_adder full_adder_3 (
    .A(A[2]), .B(B[2]), .Carry_in_b536e4fd(full_adder_2_carry_out_0c8372ad),
    .Carry_out_0c8372ad(full_adder_3_carry_out_0c8372ad), .Result(Result[2]));
  Full_adder full_adder_4 (
    .A(A[3]), .B(B[3]), .Carry_in_b536e4fd(full_adder_3_carry_out_0c8372ad),
    .Carry_out_0c8372ad(full_adder_4_carry_out_0c8372ad), .Result(Result[3]));
  Full_adder full_adder_5 (
    .A(A[4]), .B(B[4]), .Carry_in_b536e4fd(full_adder_4_carry_out_0c8372ad),
    .Carry_out_0c8372ad(full_adder_5_carry_out_0c8372ad), .Result(Result[4]));
  Full_adder full_adder_6 (
    .A(A[5]), .B(B[5]), .Carry_in_b536e4fd(full_adder_5_carry_out_0c8372ad),
    .Carry_out_0c8372ad(full_adder_6_carry_out_0c8372ad), .Result(Result[5]));
  Full_adder full_adder_7 (
    .A(A[6]), .B(B[6]), .Carry_in_b536e4fd(full_adder_6_carry_out_0c8372ad),
    .Carry_out_0c8372ad(full_adder_7_carry_out_0c8372ad), .Result(Result[6]));
  Full_adder full_adder_8 (
    .A(A[7]), .B(B[7]), .Carry_in_b536e4fd(full_adder_7_carry_out_0c8372ad),
    .Carry_out_0c8372ad(full_adder_8_carry_out_0c8372ad), .Result(Result[7]));
  Full_adder full_adder_9 (
    .A(A[8]), .B(B[8]), .Carry_in_b536e4fd(full_adder_8_carry_out_0c8372ad),
    .Carry_out_0c8372ad(full_adder_9_carry_out_0c8372ad), .Result(Result[8]));
  Full_adder full_adder_10 (
    .A(A[9]), .B(B[9]), .Carry_in_b536e4fd(full_adder_9_carry_out_0c8372ad),
    .Carry_out_0c8372ad(full_adder_10_carry_out_0c8372ad), .Result(Result[9]));
  Full_adder full_adder_11 (
    .A(A[10]), .B(B[10]), .Carry_in_b536e4fd(full_adder_10_carry_out_0c8372ad),
    .Carry_out_0c8372ad(full_adder_11_carry_out_0c8372ad), .Result(Result[10]));
  Full_adder full_adder_12 (
    .A(A[11]), .B(B[11]), .Carry_in_b536e4fd(full_adder_11_carry_out_0c8372ad),
    .Carry_out_0c8372ad(full_adder_12_carry_out_0c8372ad), .Result(Result[11]));
  Full_adder full_adder_13 (
    .A(A[12]), .B(B[12]), .Carry_in_b536e4fd(full_adder_12_carry_out_0c8372ad),
    .Carry_out_0c8372ad(full_adder_13_carry_out_0c8372ad), .Result(Result[12]));
  Full_adder full_adder_14 (
    .A(A[13]), .B(B[13]), .Carry_in_b536e4fd(full_adder_13_carry_out_0c8372ad),
    .Carry_out_0c8372ad(full_adder_14_carry_out_0c8372ad), .Result(Result[13]));
  Full_adder full_adder_15 (
    .A(A[14]), .B(B[14]), .Carry_in_b536e4fd(full_adder_14_carry_out_0c8372ad),
    .Carry_out_0c8372ad(full_adder_15_carry_out_0c8372ad), .Result(Result[14]));
  Full_adder full_adder_16 (
    .A(A[15]), .B(B[15]), .Carry_in_b536e4fd(full_adder_15_carry_out_0c8372ad),
    .Carry_out_0c8372ad(full_adder_16_carry_out_0c8372ad), .Result(Result[15]));
  Full_adder full_adder_17 (
    .A(A[16]), .B(B[16]), .Carry_in_b536e4fd(full_adder_16_carry_out_0c8372ad),
    .Carry_out_0c8372ad(full_adder_17_carry_out_0c8372ad), .Result(Result[16]));
  Full_adder full_adder_18 (
    .A(A[17]), .B(B[17]), .Carry_in_b536e4fd(full_adder_17_carry_out_0c8372ad),
    .Carry_out_0c8372ad(full_adder_18_carry_out_0c8372ad), .Result(Result[17]));
  Full_adder full_adder_19 (
    .A(A[18]), .B(B[18]), .Carry_in_b536e4fd(full_adder_18_carry_out_0c8372ad),
    .Carry_out_0c8372ad(full_adder_19_carry_out_0c8372ad), .Result(Result[18]));
  Full_adder full_adder_20 (
    .A(A[19]), .B(B[19]), .Carry_in_b536e4fd(full_adder_19_carry_out_0c8372ad),
    .Carry_out_0c8372ad(full_adder_20_carry_out_0c8372ad), .Result(Result[19]));
  Full_adder full_adder_21 (
    .A(A[20]), .B(B[20]), .Carry_in_b536e4fd(full_adder_20_carry_out_0c8372ad),
    .Carry_out_0c8372ad(full_adder_21_carry_out_0c8372ad), .Result(Result[20]));
  Full_adder full_adder_22 (
    .A(A[21]), .B(B[21]), .Carry_in_b536e4fd(full_adder_21_carry_out_0c8372ad),
    .Carry_out_0c8372ad(full_adder_22_carry_out_0c8372ad), .Result(Result[21]));
  Full_adder full_adder_23 (
    .A(A[22]), .B(B[22]), .Carry_in_b536e4fd(full_adder_22_carry_out_0c8372ad),
    .Carry_out_0c8372ad(full_adder_23_carry_out_0c8372ad), .Result(Result[22]));
  Full_adder full_adder_24 (
    .A(A[23]), .B(B[23]), .Carry_in_b536e4fd(full_adder_23_carry_out_0c8372ad),
    .Carry_out_0c8372ad(full_adder_24_carry_out_0c8372ad), .Result(Result[23]));
  Full_adder full_adder_25 (
    .A(A[24]), .B(B[24]), .Carry_in_b536e4fd(full_adder_24_carry_out_0c8372ad),
    .Carry_out_0c8372ad(full_adder_25_carry_out_0c8372ad), .Result(Result[24]));
  Full_adder full_adder_26 (
    .A(A[25]), .B(B[25]), .Carry_in_b536e4fd(full_adder_25_carry_out_0c8372ad),
    .Carry_out_0c8372ad(full_adder_26_carry_out_0c8372ad), .Result(Result[25]));
  Full_adder full_adder_27 (
    .A(A[26]), .B(B[26]), .Carry_in_b536e4fd(full_adder_26_carry_out_0c8372ad),
    .Carry_out_0c8372ad(full_adder_27_carry_out_0c8372ad), .Result(Result[26]));
  Full_adder full_adder_28 (
    .A(A[27]), .B(B[27]), .Carry_in_b536e4fd(full_adder_27_carry_out_0c8372ad),
    .Carry_out_0c8372ad(full_adder_28_carry_out_0c8372ad), .Result(Result[27]));
  Full_adder full_adder_29 (
    .A(A[28]), .B(B[28]), .Carry_in_b536e4fd(full_adder_28_carry_out_0c8372ad),
    .Carry_out_0c8372ad(full_adder_29_carry_out_0c8372ad), .Result(Result[28]));
  Full_adder full_adder_30 (
    .A(A[29]), .B(B[29]), .Carry_in_b536e4fd(full_adder_29_carry_out_0c8372ad),
    .Carry_out_0c8372ad(full_adder_30_carry_out_0c8372ad), .Result(Result[29]));
  Full_adder full_adder_31 (
    .A(A[30]), .B(B[30]), .Carry_in_b536e4fd(full_adder_30_carry_out_0c8372ad),
    .Carry_out_0c8372ad(full_adder_31_carry_out_0c8372ad), .Result(Result[30]));
  Full_adder full_adder_32 (
    .A(A[31]), .B(B[31]), .Carry_in_b536e4fd(full_adder_31_carry_out_0c8372ad), .Carry_out_0c8372ad(Carry),
    .Result(Result[31]));

  // Other names for the same wires on the sheet: res0 = Result[0]; res1 = Result[1]
endmodule

module L_32_bit_xor_40cd5d75 (
  input  Control,
  input  [31:0] B,
  output [31:0] Result
);

  wire [31:0] bit_extender_1_out;

  assign bit_extender_1_out = {{31{Control}}, Control};  // Bit_Extender bit_extender_1
  assign Result = bit_extender_1_out ^ B;  // XOR_Gate xor_1, 32 bits wide
endmodule

// 32-bit \nADD/SUB
module Add_sub (
  input  Sub,
  input  [31:0] A,
  input  [31:0] B,
  output [31:0] Result,
  output Carry,
  output Overflow
);

  wire and_1_out, and_2_out, l_31th_bit_out_54576267_1_l_31th_bit_03e70a82,
       l_31th_bit_out_54576267_2_l_31th_bit_03e70a82, l_31th_bit_out_54576267_3_l_31th_bit_03e70a82,
       not_1_out, not_2_out, not_3_out;
  wire [31:0] l_32_bit_xor_40cd5d75_1_result;

  L_31th_bit_out_54576267 l_31th_bit_out_54576267_1 (
    .Input(A), .L_31th_bit_03e70a82(l_31th_bit_out_54576267_1_l_31th_bit_03e70a82));
  not not_1 (not_1_out, l_31th_bit_out_54576267_1_l_31th_bit_03e70a82);
  L_31th_bit_out_54576267 l_31th_bit_out_54576267_2 (
    .Input(l_32_bit_xor_40cd5d75_1_result),
    .L_31th_bit_03e70a82(l_31th_bit_out_54576267_2_l_31th_bit_03e70a82));
  not not_2 (not_2_out, l_31th_bit_out_54576267_2_l_31th_bit_03e70a82);
  L_32_bit_xor_40cd5d75 l_32_bit_xor_40cd5d75_1 (.Control(Sub), .B(B), .Result(l_32_bit_xor_40cd5d75_1_result));
  L_32_bit_full_adder_concise_37212314 l_32_bit_full_adder_concise_37212314_1 (
    .A(A), .B(l_32_bit_xor_40cd5d75_1_result), .Carry_in_b536e4fd(Sub), .Result(Result), .Carry(Carry));
  L_31th_bit_out_54576267 l_31th_bit_out_54576267_3 (
    .Input(Result), .L_31th_bit_03e70a82(l_31th_bit_out_54576267_3_l_31th_bit_03e70a82));
  not not_3 (not_3_out, l_31th_bit_out_54576267_3_l_31th_bit_03e70a82);
  and and_1 (and_1_out, not_3_out, l_31th_bit_out_54576267_2_l_31th_bit_03e70a82, l_31th_bit_out_54576267_1_l_31th_bit_03e70a82);
  and and_2 (and_2_out, l_31th_bit_out_54576267_3_l_31th_bit_03e70a82, not_2_out, not_1_out);
  or or_1 (Overflow, and_1_out, and_2_out);

  // Notes on the sheet:
  //   A31
  //   B31
  //   Result 31
endmodule

// 31th
module L_31th_bit_out_54576267 (
  input  [31:0] Input,
  output L_31th_bit_03e70a82
);


  assign L_31th_bit_03e70a82 = Input[31];
endmodule

// Reduce-OR
module L_32_bit_reduce_or_303f46c2 (
  input  [31:0] Input,
  output Output
);

  or or_1 (Output, Input[0], Input[1], Input[2], Input[3], Input[4], Input[5], Input[6], Input[7], Input[8], Input[9], Input[10], Input[11], Input[12], Input[13], Input[14], Input[15], Input[17], Input[18], Input[19], Input[20], Input[21], Input[22], Input[23], Input[24], Input[25], Input[26], Input[27], Input[28], Input[29], Input[30], Input[31], Input[16]);
endmodule
